# Fritzing sketch Untitled Sketch 2 (saved by Fritzing 0.9.3b)
breadboards: 2

parts:
  IC2 = IC, DIP package, 14 pins [chip_label=7420]
  IC3 = IC, DIP package, 14 pins [chip_label=7400]
  IC1 = IC, DIP package, 14 pins [chip_label=7400]
  IC4 = IC, DIP package, 14 pins [chip_label=7400]
  IC5 = IC, DIP package, 14 pins [chip_label=7420]

nets:
  N1: IC2.pin1, IC1.pin6
  N2: IC2.pin2, IC2.pin5, IC1.pin12, IC1.pin13
  N3: IC2.pin3, IC3.pin1
  N4: IC2.pin4, IC1.pin3
  N5: IC2.pin6, IC3.pin12
  N6: IC2.pin7, IC3.pin7, IC1.pin7
  N7: IC2.pin8, IC3.pin13
  N8: IC2.pin9, IC1.pin11
  N9: IC2.pin10, IC2.pin11
  N10: IC2.pin12, IC2.pin13, IC1.pin8
  N11: IC2.pin14, IC3.pin14, IC1.pin14
  N12: IC3.pin2, IC3.pin8
  N13: IC3.pin9, IC3.pin10, IC3.pin11
  N14: IC1.pin2, IC1.pin9
  N15: IC1.pin4, IC1.pin5, IC1.pin10
  N16: IC4.pin1, IC5.pin4
  N17: IC4.pin2, IC5.pin1
  N18: IC4.pin3, IC4.pin4, IC4.pin7, IC5.pin5, IC5.pin7
  N19: IC4.pin5, IC4.pin6, IC4.pin12
  N20: IC4.pin10, IC5.pin6
  N21: IC4.pin11, IC5.pin2
  N22: IC4.pin13, IC4.pin14, IC5.pin14
