# Fritzing sketch Untitled Sketch 3 (saved by Fritzing 0.9.3b)
breadboards: 1

parts:
  IC1 = IC, DIP package, 14 pins [chip_label=7420]
  IC2 = IC, DIP package, 14 pins [chip_label=7400]
  IC3 = IC, DIP package, 14 pins [chip_label=7400]

nets:
  N1: IC1.pin5, IC2.pin3
  N2: IC1.pin6, IC2.pin12, IC2.pin13, IC3.pin13
  N3: IC1.pin7, IC2.pin7, IC3.pin7
  N4: IC1.pin14, IC2.pin14, IC3.pin14
  N5: IC2.pin1, IC2.pin2
  N6: IC2.pin4, IC2.pin8
  N7: IC2.pin10, IC2.pin11
  N8: IC3.pin9, IC3.pin10, IC3.pin11
