# Fritzing sketch Untitled Sketch (saved by Fritzing 0.9.3b)
breadboards: 1

parts:
  IC2 = IC, DIP package, 14 pins [chip_label=7420]
  IC3 = IC, DIP package, 14 pins [chip_label=7420]
  IC4 = IC, DIP package, 14 pins [chip_label=7400]

nets:
  N1: IC2.pin1, IC4.pin12
  N2: IC2.pin4, IC3.pin4, IC4.pin3
  N3: IC2.pin6, IC2.pin9
  N4: IC2.pin7, IC3.pin7, IC4.pin7
  N5: IC2.pin10, IC3.pin6
  N6: IC2.pin12, IC3.pin8
  N7: IC2.pin13, IC2.pin14, IC3.pin1, IC3.pin13, IC3.pin14, IC4.pin14
  N8: IC3.pin2, IC3.pin12, IC4.pin11
  N9: IC3.pin5, IC3.pin9, IC4.pin6
  N10: IC3.pin10, IC4.pin1, IC4.pin2
  N11: IC4.pin4, IC4.pin5
