# Fritzing sketch Untitled Sketch 2 (saved by Fritzing 0.9.3b)
breadboards: 2

parts:
  IC1 = IC, DIP package, 16 pins [chip_label=74151]
  IC2 = IC, DIP package, 14 pins [chip_label=7400]
  IC3 = IC, DIP package, 16 pins [chip_label=74138]
  IC4 = IC, DIP package, 14 pins [chip_label=7420]
  IC5 = IC, DIP package, 14 pins [chip_label=7400]

nets:
  N1: IC1.pin1, IC1.pin3, IC1.pin7, IC1.pin8, IC2.pin7
  N2: IC1.pin2, IC1.pin13, IC1.pin14, IC2.pin14
  N3: IC1.pin4, IC2.pin11
  N4: IC1.pin12, IC1.pin15, IC2.pin12, IC2.pin13
  N5: IC3.pin4, IC3.pin5, IC3.pin8, IC4.pin7, IC5.pin7
  N6: IC3.pin6, IC3.pin16, IC4.pin14, IC5.pin14
  N7: IC3.pin7, IC4.pin9
  N8: IC3.pin9, IC4.pin10, IC5.pin13
  N9: IC3.pin10, IC4.pin4
  N10: IC3.pin11, IC4.pin2
  N11: IC3.pin12, IC4.pin1
  N12: IC3.pin14, IC4.pin12
  N13: IC3.pin15, IC4.pin13
  N14: IC4.pin5, IC5.pin8
  N15: IC5.pin9, IC5.pin11
