# Fritzing sketch 138 (saved by Fritzing 0.9.3b)
breadboards: 1

parts:
  IC2 = IC, DIP package, 14 pins [chip_label=7420]
  IC1 = IC, DIP package, 16 pins [chip_label=74138]

nets:
  N1: IC2.pin4, IC1.pin10
  N2: IC2.pin5, IC1.pin9
  N3: IC2.pin7, IC1.pin8
  N4: IC2.pin9, IC1.pin11
  N5: IC2.pin10, IC1.pin12
  N6: IC2.pin12, IC1.pin13
  N7: IC2.pin13, IC1.pin14
  N8: IC2.pin14, IC1.pin16
