# Fritzing sketch 138ZZ (saved by Fritzing 0.9.3b)
breadboards: 1

parts:
  IC5 = IC, DIP package, 16 pins [chip_label=74151]
  IC6 = IC, DIP package, 16 pins [chip_label=74151]

nets:
  N1: IC5.pin1, IC5.pin2, IC5.pin3, IC5.pin15, IC5.pin16, IC6.pin2, IC6.pin3, IC6.pin13, IC6.pin14, IC6.pin16
  N2: IC5.pin4, IC5.pin7, IC5.pin8, IC5.pin12, IC5.pin13, IC5.pin14, IC6.pin1, IC6.pin4, IC6.pin7, IC6.pin8, IC6.pin12, IC6.pin15
  N3: IC5.pin9, IC6.pin9
  N4: IC5.pin10, IC6.pin10
  N5: IC5.pin11, IC6.pin11

notes:
  A0A1A2
  B1B0B2
