# Fritzing sketch 151 (saved by Fritzing 0.9.3b)
breadboards: 1

parts:
  IC2 = IC, DIP package, 16 pins [chip_label=74151]
  IC3 = IC, DIP package, 16 pins [chip_label=74151]
  IC4 = IC, DIP package, 16 pins [chip_label=74151]

nets:
  N1: IC2.pin1, IC2.pin2, IC2.pin3, IC3.pin2, IC3.pin3, IC4.pin1, IC4.pin3, IC4.pin12, IC4.pin14, IC4.pin16
  N2: IC2.pin4, IC3.pin1, IC3.pin4, IC4.pin2, IC4.pin4, IC4.pin8, IC4.pin13, IC4.pin15
