# Fritzing sketch 1 (saved by Fritzing 0.9.3b)
breadboards: 1

parts:
  IC1 = IC, DIP package, 14 pins [chip_label=74HC00]
  IC2 = IC, DIP package, 14 pins [chip_label=74HC20]
  IC3 = IC, DIP package, 14 pins [chip_label=74HC20]
  IC4 = IC, DIP package, 14 pins [chip_label=74HC00]
  IC6 = IC, DIP package, 14 pins [chip_label=74HC20]
  IC5 = IC, DIP package, 14 pins [chip_label=74HC20]

nets:
  N1: IC1.pin1, IC1.pin5, IC1.pin8, IC2.pin1, IC2.pin5, IC3.pin4, IC4.pin1, IC4.pin5, IC4.pin8, IC6.pin4, IC5.pin1, IC5.pin5
  N2: IC1.pin2, IC2.pin2, IC4.pin2, IC5.pin2
  N3: IC1.pin3, IC2.pin3, IC3.pin12, IC4.pin3, IC6.pin12, IC5.pin3
  N4: IC1.pin4, IC2.pin4, IC4.pin4, IC5.pin4
  N5: IC1.pin6, IC2.pin6, IC2.pin9, IC3.pin2, IC4.pin6, IC6.pin2, IC5.pin6, IC5.pin9
  N6: IC1.pin7, IC2.pin7, IC3.pin7, IC4.pin7, IC6.pin7, IC5.pin7
  N7: IC1.pin9, IC2.pin12, IC3.pin13, IC4.pin9, IC6.pin13, IC5.pin12
  N8: IC1.pin10, IC1.pin13, IC1.pin14, IC2.pin10, IC2.pin14, IC3.pin9, IC3.pin10, IC3.pin14, IC4.pin10, IC4.pin13, IC4.pin14, IC6.pin9, IC6.pin10, IC6.pin14, IC5.pin10, IC5.pin14
  N9: IC1.pin11, IC2.pin13, IC4.pin11, IC5.pin13
  N10: IC1.pin12, IC4.pin12
  N11: IC2.pin8, IC3.pin1, IC6.pin1, IC5.pin8
  N12: IC2.pin11, IC5.pin11
  N13: IC3.pin3, IC6.pin3
  N14: IC3.pin5, IC3.pin8, IC6.pin5, IC6.pin8
  N15: IC3.pin6, IC6.pin6
  N16: IC3.pin11, IC6.pin11
