# Fritzing sketch 4.1.1 (saved by Fritzing 0.9.3b)
breadboards: 1

parts:
  IC1 = IC, DIP package, 14 pins [chip_label=74HC20]
  IC2 = IC, DIP package, 14 pins [chip_label=74HC04]
  IC3 = IC, DIP package, 14 pins [chip_label=74HC00]
  IC4 = IC, DIP package, 14 pins [chip_label=7486]

nets:
  N1: IC1.pin2, IC3.pin8
  N2: IC1.pin4, IC3.pin11
  N3: IC1.pin5, IC1.pin8
  N4: IC1.pin7, IC2.pin7, IC3.pin7, IC4.pin7
  N5: IC1.pin9, IC1.pin14, IC2.pin14, IC3.pin14, IC4.pin14
  N6: IC1.pin10, IC2.pin8
  N7: IC1.pin12, IC2.pin10
  N8: IC1.pin13, IC2.pin13
  N9: IC2.pin9, IC3.pin12, IC4.pin12
  N10: IC2.pin11, IC3.pin9, IC4.pin13
  N11: IC2.pin12, IC3.pin10, IC3.pin13
