# Fritzing sketch 4.1.2 (saved by Fritzing 0.9.3b)
breadboards: 1

parts:
  IC1 = IC, DIP package, 16 pins [chip_label=74HC151]
  IC2 = IC, DIP package, 14 pins [chip_label=7486]

nets:
  N1: IC1.pin1, IC1.pin2, IC1.pin3
  N2: IC1.pin4, IC1.pin7, IC1.pin8, IC2.pin7
  N3: IC1.pin9, IC2.pin12
  N4: IC1.pin10, IC2.pin13
  N5: IC1.pin12, IC1.pin13, IC1.pin14
  N6: IC1.pin15, IC1.pin16, IC2.pin14
