# Fritzing sketch 4.1.3 (saved by Fritzing 0.9.3b)
breadboards: 1

parts:
  IC1 = IC, DIP package, 16 pins [chip_label=74HC138]
  IC2 = IC, DIP package, 14 pins [chip_label=74HC20]
  IC3 = IC, DIP package, 14 pins [chip_label=74HC86]

nets:
  N1: IC1.pin2, IC3.pin1
  N2: IC1.pin3, IC3.pin2
  N3: IC1.pin4, IC1.pin5, IC1.pin8, IC2.pin7, IC3.pin7
  N4: IC1.pin11, IC2.pin9
  N5: IC1.pin12, IC2.pin10
  N6: IC1.pin13, IC2.pin12
  N7: IC1.pin14, IC2.pin13
  N8: IC1.pin16, IC2.pin14, IC3.pin14
