# Fritzing sketch Untitled Sketch 2 (saved by Fritzing 0.9.3b)
breadboards: 1

parts:
  IC1 = IC, DIP package, 16 pins [chip_label=74151]

nets:
  N1: IC1.pin1, IC1.pin2, IC1.pin12
  N2: IC1.pin3, IC1.pin4
  N3: IC1.pin7, IC1.pin8
  N4: IC1.pin13, IC1.pin15
  N5: IC1.pin14, IC1.pin16
