# Fritzing sketch Untitled Sketch 3 (saved by Fritzing 0.9.3b)
breadboards: 1

parts:
  IC1 = IC, DIP package, 16 pins [chip_label=74138]
  IC2 = IC, DIP package, 14 pins [chip_label=7400]
  IC3 = IC, DIP package, 14 pins [chip_label=7420]

nets:
  N1: IC1.pin4, IC1.pin5, IC1.pin8, IC2.pin7, IC3.pin7
  N2: IC1.pin7, IC3.pin5, IC3.pin9
  N3: IC1.pin9, IC3.pin4, IC3.pin10
  N4: IC1.pin10, IC3.pin2
  N5: IC1.pin11, IC2.pin12
  N6: IC1.pin12, IC2.pin13
  N7: IC1.pin13, IC3.pin12
  N8: IC1.pin14, IC3.pin13
  N9: IC1.pin16, IC2.pin9, IC2.pin14, IC3.pin14
  N10: IC2.pin8, IC3.pin1
  N11: IC2.pin10, IC2.pin11
