# Fritzing sketch Untitled Sketch 2 (saved by Fritzing 0.9.3b)
breadboards: 1

parts:
  IC1 = IC, DIP package, 14 pins [chip_label=7474]
  IC2 = IC, DIP package, 14 pins [chip_label=7474]
  IC3 = IC, DIP package, 14 pins [chip_label=7400]
  IC4 = IC, DIP package, 14 pins [chip_label=7486]
  IC5 = IC, DIP package, 16 pins [chip_label=74138]

nets:
  N1: IC1.pin1, IC1.pin4, IC2.pin1, IC2.pin4, IC5.pin6
  N2: IC1.pin2, IC4.pin3
  N3: IC1.pin5, IC4.pin2, IC5.pin3
  N4: IC1.pin7, IC2.pin7, IC3.pin7, IC4.pin7, IC5.pin4, IC5.pin5, IC5.pin8
  N5: IC1.pin14, IC2.pin10, IC2.pin13, IC2.pin14, IC3.pin9, IC3.pin14, IC4.pin14, IC5.pin16
  N6: IC2.pin2, IC2.pin6
  N7: IC2.pin5, IC3.pin12, IC4.pin12, IC5.pin1
  N8: IC2.pin9, IC3.pin13, IC4.pin13, IC5.pin2
  N9: IC2.pin12, IC4.pin11
  N10: IC3.pin8, IC4.pin1
  N11: IC3.pin10, IC3.pin11
