# Fritzing sketch 流水灯 (saved by Fritzing 0.9.3b)
breadboards: 1

parts:
  IC1 = IC, DIP package, 16 pins [chip_label=74161]
  IC2 = IC, DIP package, 16 pins [chip_label=74138]
  IC3 = IC, DIP package, 14 pins [chip_label=7400]

nets:
  N1: IC1.pin1, IC3.pin6
  N2: IC1.pin7, IC2.pin6
  N3: IC1.pin8, IC2.pin4, IC2.pin5, IC2.pin8, IC3.pin7
  N4: IC1.pin9, IC1.pin10, IC1.pin16, IC2.pin16, IC3.pin8, IC3.pin14
  N5: IC1.pin11, IC3.pin5
  N6: IC1.pin12, IC2.pin3
  N7: IC1.pin13, IC2.pin2
  N8: IC1.pin14, IC2.pin1
