# Fritzing sketch Untitled Sketch 3 (saved by Fritzing 0.9.3b)
breadboards: 1

parts:
  IC9 = IC, DIP package, 14 pins [chip_label=7486]
  IC10 = IC, DIP package, 14 pins [chip_label=7400]
  IC11 = IC, DIP package, 16 pins [chip_label=74194]
  IC12 = IC, DIP package, 16 pins [chip_label=74151]
  IC13 = IC, DIP package, 16 pins [chip_label=74161]

nets:
  N1: IC9.pin1, IC12.pin5
  N2: IC9.pin2, IC11.pin11, IC13.pin2
  N3: IC9.pin7, IC10.pin7, IC11.pin8, IC12.pin7, IC12.pin8, IC13.pin3, IC13.pin4, IC13.pin5, IC13.pin6, IC13.pin8
  N4: IC9.pin14, IC10.pin14, IC11.pin16, IC12.pin16, IC13.pin10, IC13.pin16
  N5: IC10.pin8, IC11.pin9, IC11.pin10
  N6: IC10.pin9, IC10.pin10, IC10.pin11, IC13.pin9
  N7: IC10.pin12, IC12.pin10, IC13.pin13
  N8: IC10.pin13, IC12.pin11, IC13.pin14
  N9: IC11.pin1, IC11.pin2, IC11.pin7, IC13.pin1, IC13.pin7
  N10: IC11.pin12, IC12.pin1
  N11: IC11.pin13, IC12.pin2
  N12: IC11.pin14, IC12.pin3
  N13: IC11.pin15, IC12.pin4
  N14: IC12.pin9, IC13.pin12
  N15: IC12.pin12, IC12.pin13, IC12.pin14, IC12.pin15
