# Fritzing sketch Untitled Sketch 2 (saved by Fritzing 0.9.3b)
breadboards: 1

parts:
  IC1 = IC, DIP package, 16 pins [chip_label=74161]
  IC2 = IC, DIP package, 16 pins [chip_label=74138]
  IC3 = IC, DIP package, 14 pins [chip_label=7420]
  IC4 = IC, DIP package, 14 pins [chip_label=7404]
  IC5 = IC, DIP package, 14 pins [chip_label=7400]

nets:
  N1: IC1.pin1, IC1.pin7, IC2.pin6
  N2: IC1.pin3, IC1.pin4, IC1.pin5, IC1.pin6, IC1.pin8, IC2.pin4, IC2.pin5, IC2.pin8, IC3.pin1, IC3.pin7, IC4.pin7, IC5.pin7
  N3: IC1.pin9, IC5.pin8
  N4: IC1.pin10, IC1.pin16, IC2.pin16, IC3.pin12, IC3.pin14, IC4.pin14, IC5.pin9, IC5.pin14
  N5: IC1.pin12, IC3.pin4
  N6: IC1.pin13, IC3.pin10
  N7: IC1.pin14, IC3.pin9
  N8: IC1.pin15, IC2.pin1, IC3.pin5
  N9: IC2.pin10, IC5.pin5
  N10: IC2.pin11, IC5.pin2
  N11: IC2.pin12, IC4.pin11
  N12: IC2.pin13, IC5.pin1
  N13: IC2.pin14, IC5.pin4
  N14: IC2.pin15, IC4.pin13
  N15: IC3.pin6, IC5.pin12
  N16: IC3.pin8, IC5.pin13
  N17: IC5.pin10, IC5.pin11
