# Fritzing sketch 数值判别 (saved by Fritzing 0.9.3b)
breadboards: 1

parts:
  IC1 = IC, DIP package, 14 pins [chip_label=74HC00]
  IC2 = IC, DIP package, 14 pins [chip_label=74HC00]
  IC3 = IC, DIP package, 14 pins [chip_label=74HC20]
  IC4 = IC, DIP package, 14 pins [chip_label=74HC20]

nets:
  N1: IC1.pin1, IC1.pin4, IC1.pin7, IC2.pin7, IC3.pin2, IC3.pin4, IC3.pin7, IC4.pin1, IC4.pin7
  N2: IC1.pin2, IC3.pin12
  N3: IC1.pin3, IC3.pin1
  N4: IC1.pin5, IC3.pin9
  N5: IC1.pin6, IC4.pin9
  N6: IC1.pin11, IC3.pin13
  N7: IC1.pin12, IC3.pin5, IC4.pin10
  N8: IC1.pin13, IC1.pin14, IC2.pin14, IC3.pin10, IC3.pin14, IC4.pin12, IC4.pin13, IC4.pin14
  N9: IC3.pin6, IC4.pin2
  N10: IC3.pin8, IC4.pin4
  N11: IC4.pin5, IC4.pin8

notes:
  b
  c
  d
