# Fritzing sketch 数字锁 (saved by Fritzing 0.9.3b)
breadboards: 1

parts:
  IC3 = IC, DIP package, 14 pins [chip_label=74HC20]
  IC4 = IC, DIP package, 14 pins [chip_label=74HC00]
  IC5 = IC, DIP package, 14 pins [chip_label=74HC04]

nets:
  N1: IC3.pin6, IC4.pin1
  N2: IC3.pin7, IC4.pin7, IC5.pin7
  N3: IC3.pin14, IC4.pin14, IC5.pin14
  N4: IC4.pin2, IC4.pin4
  N5: IC4.pin3, IC4.pin5, IC5.pin1
  N6: IC4.pin6, IC5.pin13
