# Fritzing sketch 供电控制 (saved by Fritzing 0.9.3b)
breadboards: 1

parts:
  IC5 = IC, DIP package, 16 pins [chip_label=74138]
  IC6 = IC, DIP package, 14 pins [chip_label=7420]
  IC7 = IC, DIP package, 14 pins [chip_label=7430]

nets:
  N1: IC5.pin4, IC5.pin5, IC5.pin8, IC6.pin7, IC7.pin7
  N2: IC5.pin6, IC5.pin16, IC6.pin14, IC7.pin4, IC7.pin5, IC7.pin6, IC7.pin14
  N3: IC5.pin7, IC6.pin9, IC7.pin3
  N4: IC5.pin9, IC6.pin10, IC7.pin12
  N5: IC5.pin10, IC7.pin2
  N6: IC5.pin11, IC7.pin1
  N7: IC5.pin12, IC7.pin11
  N8: IC5.pin13, IC6.pin12
  N9: IC5.pin14, IC6.pin13

notes:
  A
  C
  B
  K0
  K1
