# Fritzing sketch 血型配对 (saved by Fritzing 0.9.3b)
breadboards: 1

parts:
  IC3 = IC, DIP package, 14 pins [chip_label=7404]
  IC4 = IC, DIP package, 14 pins [chip_label=7408]
  IC8 = IC, DIP package, 16 pins [chip_label=74153]

nets:
  N1: IC3.pin5, IC8.pin4
  N2: IC3.pin6, IC8.pin3, IC8.pin5, IC8.pin6
  N3: IC3.pin7, IC4.pin7, IC8.pin8, IC8.pin10, IC8.pin11
  N4: IC3.pin8, IC8.pin15
  N5: IC3.pin9, IC8.pin1
  N6: IC3.pin14, IC4.pin14, IC8.pin12, IC8.pin13, IC8.pin16
  N7: IC4.pin1, IC8.pin7
  N8: IC4.pin2, IC8.pin9

notes:
  A
  B
  C
  D
  K
