# Fritzing sketch 补码1 (saved by Fritzing 0.9.3b)
breadboards: 1

parts:
  IC1 = IC, DIP package, 14 pins [chip_label=7404]
  IC1_2 = IC, DIP package, 14 pins [chip_label=7404]
  IC2 = IC, DIP package, 14 pins [chip_label=7486]
  IC3 = IC, DIP package, 14 pins [chip_label=7400]

nets:
  N1: IC1.pin1, IC1_2.pin1
  N2: IC1.pin2, IC1_2.pin2
  N3: IC1.pin3, IC1_2.pin3, IC2.pin9
  N4: IC1.pin4, IC1_2.pin4
  N5: IC1.pin5, IC1_2.pin5, IC3.pin5, IC3.pin11
  N6: IC1.pin6, IC1_2.pin6, IC3.pin9
  N7: IC1.pin7, IC1_2.pin7, IC2.pin3, IC3.pin13
  N8: IC1.pin8, IC1.pin11, IC1_2.pin8, IC1_2.pin11, IC2.pin7, IC3.pin7
  N9: IC1.pin9, IC1_2.pin9
  N10: IC1.pin10, IC1_2.pin10
  N11: IC1.pin12, IC1_2.pin12
  N12: IC1.pin13, IC1_2.pin13
  N13: IC1.pin14, IC1_2.pin14
  N14: IC2.pin1, IC2.pin12
  N15: IC2.pin2, IC3.pin1
  N16: IC2.pin13, IC3.pin2
  N17: IC3.pin3, IC3.pin4

notes:
  B0(Y0)
  B2
  B1
  Y2
  Y1
