# Fritzing sketch 补码2 (saved by Fritzing 0.9.3b)
breadboards: 1

parts:
  IC2 = IC, DIP package, 14 pins [chip_label=7404]
  IC6 = IC, DIP package, 14 pins [chip_label=7432]
  IC3 = IC, DIP package, 16 pins [chip_label=74153]
  IC7 = IC, DIP package, 16 pins [chip_label=74153]
  IC8 = IC, DIP package, 16 pins [chip_label=74153]

nets:
  N1: IC2.pin7, IC6.pin4, IC6.pin7, IC3.pin6, IC3.pin8, IC3.pin11, IC3.pin12, IC3.pin13, IC7.pin3, IC7.pin6, IC7.pin8, IC7.pin10, IC8.pin4, IC8.pin6, IC8.pin8, IC8.pin10, IC8.pin12
  N2: IC2.pin12, IC3.pin15, IC7.pin15, IC8.pin15
  N3: IC2.pin13, IC3.pin1, IC7.pin1, IC8.pin1
  N4: IC2.pin14, IC6.pin14, IC3.pin3, IC3.pin4, IC3.pin5, IC3.pin10, IC3.pin16, IC7.pin4, IC7.pin5, IC7.pin11, IC7.pin12, IC7.pin13, IC7.pin16, IC8.pin3, IC8.pin5, IC8.pin11, IC8.pin13, IC8.pin16
  N5: IC6.pin1, IC7.pin9
  N6: IC6.pin2, IC7.pin7
  N7: IC6.pin5, IC8.pin9
  N8: IC6.pin12, IC3.pin7
  N9: IC6.pin13, IC3.pin9
  N10: IC3.pin2, IC7.pin2, IC8.pin2
  N11: IC3.pin14, IC7.pin14, IC8.pin14

notes:
  B1
  B2
  B0
  Y2
  Y1
  Y0
