# Fritzing sketch 补码3 (saved by Fritzing 0.9.3b)
breadboards: 1

parts:
  IC4 = IC, DIP package, 16 pins [chip_label=74138]
  IC5 = IC, DIP package, 14 pins [chip_label=7420]
  IC6 = IC, DIP package, 14 pins [chip_label=7420]

nets:
  N1: IC4.pin4, IC4.pin5, IC4.pin8, IC5.pin7, IC6.pin7
  N2: IC4.pin6, IC4.pin16, IC5.pin14, IC6.pin14
  N3: IC4.pin7, IC5.pin4, IC6.pin5
  N4: IC4.pin9, IC5.pin5, IC6.pin2
  N5: IC4.pin10, IC6.pin4
  N6: IC4.pin11, IC5.pin9
  N7: IC4.pin12, IC5.pin10
  N8: IC4.pin13, IC5.pin2, IC5.pin12
  N9: IC4.pin14, IC5.pin1, IC5.pin13, IC6.pin1

notes:
  B0
  B1
  B2
  Y2
  Y1
  Y0
